# Fritzing sketch Nano_GP2Y10_BT (saved by Fritzing 0.9.3b)
breadboards: 1

parts:
  C1 = Electrolytic Capacitor [capacitance=1µF package="100 mil [THT, electrolytic]"]
  R1 = Resistor [tolerance=±5% resistance=220 package=THT]
  U1 = Sharp Dust Sensor [part_number=GP2Y1010AU0F]  # not connected
  부품2 = Bluetooth HC-05 Macho  # not connected
  부품3 = Arduino Nano (Rev3.0)

nets:
  N1: C1.-, 부품3.GND
  N2: C1.+, R1.Pin_1, 부품3.VIN

custom parts:
  Sharp Dust Sensor: Sharp GP2Y1010AU0F Dust Sensor
