# Fritzing sketch NodeMCD_OLED_SSD1306 (saved by Fritzing 0.9.3b)

parts:
  U1 = NodeMCU V1.0
  Squix2 = OLED 0.96" 128x64 I2C SSD1306

nets:
  N1: U1.D3, Squix2.SCA
  N2: U1.D4, Squix2.SCL
  3V3: U1.3V3, Squix2.VCC
  GND: U1.GND, Squix2.GND

custom parts:
  NodeMCU V1.0: ESP8266 based NodeMCU
