# Fritzing sketch NodeMCU_GP2Y10 (saved by Fritzing 0.9.3b)
breadboards: 1

parts:
  U1 = Sharp Dust Sensor [part_number=GP2Y1010AU0F]
  C2 = Capacitor Polarized [package=cpol-radial-10uf-25v]
  U2 = NodeMCU V3.0
  R2 = Resistor [tolerance=±5% resistance=220 package=THT]

nets:
  N1: U1.V-LED, C2.+, R2.Pin_0
  N2: U1.LED-GND, U1.S-GND, C2.-
  N3: U1.LED, U2.D0, U2.D1
  N4: U1.Vo, U2.GND#41, U2.A0
  N5: U1.VCC, R2.Pin_1
  N6: U2.GND#6, U2.GND#13, U2.GND#16, U2.GND#33

custom parts:
  Sharp Dust Sensor: Sharp GP2Y1010AU0F Dust Sensor
  NodeMCU V3.0: ESP8266 based NodeMCU
