# Fritzing sketch NodeMCU_SDCard (saved by Fritzing 0.9.3b)

parts:
  U1 = NodeMCU V3.0
  microSD1 = MicroSD Card Module

nets:
  N1: U1.D5, microSD1.SCK
  N2: U1.D6, microSD1.MISO
  N3: U1.D7, microSD1.MOSI
  N4: U1.D8, microSD1.CS
  N5: U1.VU, microSD1.VCC
  GND: U1.GND, microSD1.GND

custom parts:
  NodeMCU V3.0: ESP8266 based NodeMCU
