# Fritzing sketch bread_Board0214 (saved by Fritzing 0.9.3b)
breadboards: 1

parts:
  부품1 = Bluetooth HC-05 Macho
  U1 = Sharp Dust Sensor [part_number=GP2Y1010AU0F]
  microSD1 = MicroSD Card Module
  R1 = Resistor [tolerance=±5% resistance=220 package=THT]
  C1 = Electrolytic Capacitor [capacitance=1µF package="100 mil [THT, electrolytic]"]
  OLED_I2C1 = OLED 128x64 I2C Monochrome Display  # not connected

nets:
  VCC: 부품1.VCC, U1.VCC, microSD1.VCC, R1.Pin_1, C1.+
  GND: 부품1.GND, U1.LED-GND, U1.S-GND, microSD1.GND, C1.-
  N1: U1.V-LED, R1.Pin_0

custom parts:
  Sharp Dust Sensor: Sharp GP2Y1010AU0F Dust Sensor
