# Fritzing sketch bread_Board3 (saved by Fritzing 0.9.3b)
breadboards: 1

parts:
  부품1 = Bluetooth HC-05 Macho
  U1 = Sharp Dust Sensor [part_number=GP2Y1010AU0F]  # not connected
  Grove1 = Grove OLED 128x96  # not connected
  microSD1 = MicroSD Card Module

nets:
  VCC: 부품1.VCC, microSD1.VCC
  GND: 부품1.GND, microSD1.GND

custom parts:
  Sharp Dust Sensor: Sharp GP2Y1010AU0F Dust Sensor
